// Logisim project Problem1.circ as structural Verilog: 3 circuits, main circuit main
module main (
  input  [7:0] addr,
  input  [2:0] ControlSignal
);

  wire clk_out, decode_1_o_0, decode_1_o_1, decode_1_o_2, decode_1_o_4, decode_1_o_5;
  wire [7:0] controlled_buffer_1_out, demultiplexer_1_out1, iocontroller_1_busout, RandomAccessMemory_data,
       ReadOnlyMemory_data, register_1_q;

  Clock clk (.out(clk_out));
  ROM ReadOnlyMemory (.addr(addr), .data(ReadOnlyMemory_data));
  Decode decode_1 (
    .ControlSig(ControlSignal), .O_0(decode_1_o_0), .O_1(decode_1_o_1), .O_2(decode_1_o_2),
    .O_4(decode_1_o_4), .O_5(decode_1_o_5));
  RAM #(.databus("bidir")) RandomAccessMemory (
    .addr(addr), .we(decode_1_o_2), .oe(decode_1_o_1), .clk(clk_out), .data(RandomAccessMemory_data));
  assign controlled_buffer_1_out = decode_1_o_0 ? ReadOnlyMemory_data : 8'bz;  // Controlled_Buffer controlled_buffer_1
  assign controlled_buffer_1_out = decode_1_o_1 ? RandomAccessMemory_data : 8'bz;  // Controlled_Buffer controlled_buffer_2
  Demultiplexer #(.width(8)) demultiplexer_1 (
    .out0(RandomAccessMemory_data), .out1(demultiplexer_1_out1), .in(register_1_q), .sel(decode_1_o_5));
  assign controlled_buffer_1_out = decode_1_o_4 ? iocontroller_1_busout : 8'bz;  // Controlled_Buffer controlled_buffer_3
  IOController iocontroller_1 (
    .Enable(decode_1_o_4), .addr(addr), .BusIN(demultiplexer_1_out1), .BusOUT(iocontroller_1_busout));  // open: IO_0, IO_1, IO_2, IO_3
  Register register_1 (.D(controlled_buffer_1_out), .clk(clk_out), .Q(register_1_q));  // open: en, clr

  // Notes on the sheet:
  //   000 Read from ROM
  //   001 Read from RAM
  //   010 Write to RAM
  //   011 Read from IO
  //   100 Write to IO
endmodule

module IOController (
  input  [7:0] IO_0,
  input  [7:0] IO_1,
  input  [7:0] IO_2,
  input  [7:0] IO_3,
  input  Enable,
  input  [7:0] addr,
  input  [7:0] BusIN,
  output [7:0] BusOUT
);

  wire [7:0] demultiplexer_1_out0;

  Controlled_Buffer #(.width(8)) controlled_buffer_1 (.in(demultiplexer_1_out0), .out(IO_0));  // open: en
  Multiplexer #(.select(2), .width(8)) multiplexer_1 (.out(BusOUT), .sel(addr[7:6]));  // open: in0, in1, in2, in3
  Demultiplexer #(.select(2), .width(8)) demultiplexer_1 (
    .out0(demultiplexer_1_out0), .in(BusIN), .sel(addr[7:6]));  // open: out1, out2, out3
endmodule

module Decode (
  input  [2:0] ControlSig,
  output O_0,
  output O_1,
  output O_2,
  output O_4,
  output O_5
);

  wire not_1_out, not_2_out, not_3_out;

  not not_1 (not_1_out, ControlSig[2]);
  not not_2 (not_2_out, ControlSig[1]);
  not not_3 (not_3_out, ControlSig[0]);
  and and_1 (O_0, not_1_out, not_2_out, not_3_out);
  and and_2 (O_1, not_1_out, not_2_out, ControlSig[0]);
  and and_3 (O_2, not_1_out, ControlSig[1], not_3_out);
  and and_4 (O_4, not_1_out, ControlSig[1], ControlSig[0]);
  and and_5 (O_5, ControlSig[2], not_2_out, not_3_out);
endmodule
